// Logisim project ALU.circ as structural Verilog: 12 circuits, main circuit 8bitALU
module main (
  input  in_1,
  input  in_2,
  input  in_3,
  output out_4,
  output out_5
);

  wire and_1_out, and_2_out, and_3_out;

  and and_1 (and_1_out, in_1, in_2);
  and and_2 (and_2_out, in_1, in_3);
  and and_3 (and_3_out, in_2, in_3);
  xor xor_1 (out_5, in_1, in_2, in_3);
  or or_1 (out_4, and_1_out, and_2_out, and_3_out);
endmodule

module pcb_adder (
  input  in_1,
  input  in_2,
  input  in_3,
  input  in_4,
  input  in_5,
  input  in_6,
  input  in_7,
  input  in_8,
  output out_9,
  output out_10,
  output out_11,
  output out_12,
  output out_13
);

  wire main_2_out_4, main_3_out_4, main_4_out_4;

  main main_1 (.in_1(in_1), .in_2(in_5), .in_3(main_2_out_4), .out_4(out_9), .out_5(out_10));
  main main_2 (.in_1(in_2), .in_2(in_6), .in_3(main_3_out_4), .out_4(main_2_out_4), .out_5(out_11));
  main main_3 (.in_1(in_3), .in_2(in_7), .in_3(main_4_out_4), .out_4(main_3_out_4), .out_5(out_12));
  main main_4 (.in_1(in_4), .in_2(in_8), .in_3(1'b0), .out_4(main_4_out_4), .out_5(out_13));
endmodule

module add4 (
  input  [3:0] in_1,
  input  [3:0] in_2,
  input  in_3,
  output out_4,
  output [3:0] out_5
);

  wire main_2_out_4, main_3_out_4, main_4_out_4;

  main main_1 (.in_1(in_1[0]), .in_2(in_2[0]), .in_3(main_2_out_4), .out_4(out_4), .out_5(out_5[0]));
  main main_2 (.in_1(in_1[1]), .in_2(in_2[1]), .in_3(main_3_out_4), .out_4(main_2_out_4), .out_5(out_5[1]));
  main main_3 (.in_1(in_1[2]), .in_2(in_2[2]), .in_3(main_4_out_4), .out_4(main_3_out_4), .out_5(out_5[2]));
  main main_4 (.in_1(in_1[3]), .in_2(in_2[3]), .in_3(in_3), .out_4(main_4_out_4), .out_5(out_5[3]));

  // Notes on the sheet:
  //   flip
endmodule

module _8bitALU (
  input  [7:0] a,
  input  in_2,
  input  [7:0] b,
  input  in_4,
  input  \and ,
  input  \or ,
  input  exor,
  input  lsl,
  input  rsl,
  output [7:0] out_10,
  output out_11
);

  wire [7:0] adder_1_out, and_1_out, bit_extender_1_out, leftshift8bit_1_out_2, or_1_out,
       rightshift8bit_1_out_2, xor_1_out, xor_2_out;

  assign bit_extender_1_out = {{7{1'b0}}, in_2};  // Bit_Extender bit_extender_1
  assign xor_1_out = a ^ bit_extender_1_out;  // XOR_Gate xor_1, 8 bits wide
  assign and_1_out = b & a;  // AND_Gate and_1, 8 bits wide
  assign or_1_out = b | a;  // OR_Gate or_1, 8 bits wide
  assign xor_2_out = b ^ a;  // XOR_Gate xor_2, 8 bits wide
  leftshift8bit leftshift8bit_1 (.in_1(b), .out_2(leftshift8bit_1_out_2));
  rightshift8bit rightshift8bit_1 (.in_1(b), .out_2(rightshift8bit_1_out_2));
  Adder adder_1 (.a(xor_1_out), .b(b), .out(adder_1_out), .cin(in_2), .cout(out_11));
  assign out_10 = in_4 ? adder_1_out : 8'bz;  // Controlled_Buffer controlled_buffer_1
  assign out_10 = \and  ? and_1_out : 8'bz;  // Controlled_Buffer controlled_buffer_2
  assign out_10 = \or  ? or_1_out : 8'bz;  // Controlled_Buffer controlled_buffer_3
  assign out_10 = exor ? xor_2_out : 8'bz;  // Controlled_Buffer controlled_buffer_4
  assign out_10 = lsl ? leftshift8bit_1_out_2 : 8'bz;  // Controlled_Buffer controlled_buffer_5
  assign out_10 = rsl ? rightshift8bit_1_out_2 : 8'bz;  // Controlled_Buffer controlled_buffer_6
endmodule

module _8bitadder (
  input  [7:0] in_1,
  input  [7:0] in_2,
  input  in_3,
  output out_4,
  output [7:0] out_5
);

  wire add4_2_out_4;

  add4 add4_1 (.in_1(in_1[3:0]), .in_2(in_1[7:4]), .in_3(add4_2_out_4), .out_5(out_5[3:0]), .out_4(out_4));
  add4 add4_2 (.in_1(in_2[3:0]), .in_2(in_2[7:4]), .in_3(in_3), .out_5(out_5[7:4]), .out_4(add4_2_out_4));
endmodule

module leftshift8bit (
  input  [7:0] in_1,
  output [7:0] out_2
);


  assign out_2 = {in_1[6:0], 1'b0};
endmodule

module rightshift8bit (
  input  [7:0] in_1,
  output [7:0] out_2
);


  assign out_2 = {1'b0, in_1[7:1]};
endmodule

module top (
  input  [7:0] in_1,
  input  in_2,
  input  [7:0] in_3,
  input  [7:0] in_4,
  input  in_5,
  input  in_6,
  input  in_7,
  input  in_8,
  input  in_9,
  input  in_10,
  output out_11
);

  _8bitALU u_8bitalu_1 (
    .a(in_1), .in_2(in_2), .b(in_3), .in_4(in_5), .\and (in_6), .\or (in_7), .exor(in_8), .lsl(in_9),
    .rsl(in_10), .out_10(in_4), .out_11(out_11));
endmodule

module new_alu (
  input  [7:0] a,
  input  in_2,
  input  [7:0] b,
  input  in_4,
  input  \and ,
  input  \or ,
  input  exor,
  input  lsl,
  input  rsl,
  output [7:0] out_10,
  output out_11
);

  wire [7:0] adder_1_out, and_1_out, bit_extender_1_out, leftshift8bit_1_out_2, or_1_out,
       rightshift8bit_1_out_2, xor_1_out, xor_2_out;

  assign bit_extender_1_out = {{7{1'b0}}, in_2};  // Bit_Extender bit_extender_1
  assign xor_1_out = a ^ bit_extender_1_out;  // XOR_Gate xor_1, 8 bits wide
  assign and_1_out = b & a;  // AND_Gate and_1, 8 bits wide
  assign or_1_out = b | a;  // OR_Gate or_1, 8 bits wide
  assign xor_2_out = b ^ a;  // XOR_Gate xor_2, 8 bits wide
  leftshift8bit leftshift8bit_1 (.in_1(b), .out_2(leftshift8bit_1_out_2));
  rightshift8bit rightshift8bit_1 (.in_1(b), .out_2(rightshift8bit_1_out_2));
  Adder adder_1 (.a(xor_1_out), .b(b), .out(adder_1_out), .cin(in_2), .cout(out_11));
  assign out_10 = in_4 ? adder_1_out : 8'bz;  // Controlled_Buffer controlled_buffer_1
  assign out_10 = \and  ? and_1_out : 8'bz;  // Controlled_Buffer controlled_buffer_2
  assign out_10 = \or  ? or_1_out : 8'bz;  // Controlled_Buffer controlled_buffer_3
  assign out_10 = exor ? xor_2_out : 8'bz;  // Controlled_Buffer controlled_buffer_4
  assign out_10 = lsl ? leftshift8bit_1_out_2 : 8'bz;  // Controlled_Buffer controlled_buffer_5
  assign out_10 = rsl ? rightshift8bit_1_out_2 : 8'bz;  // Controlled_Buffer controlled_buffer_6
endmodule

module alucircuit (
  input  [7:0] in_1,
  input  in_2,
  input  in_3,
  input  in_4,
  input  in_5,
  input  in_6,
  input  in_7,
  input  in_8,
  input  in_9,
  input  in_10,
  input  in_11,
  input  in_12,
  input  in_13,
  input  in_14,
  input  in_15,
  input  in_16,
  input  in_17,
  input  in_18,
  output [7:0] out_19,
  output out_20
);

  wire [7:0] controlled_buffer_1_out, controlled_buffer_2_out, register_1_q, register_2_q;

  assign controlled_buffer_1_out = in_7 ? {8{1'b0}} : 8'bz;  // Controlled_Buffer controlled_buffer_1
  assign controlled_buffer_2_out = in_2 ? in_1 : 8'bz;  // Controlled_Buffer controlled_buffer_2
  assign controlled_buffer_1_out = in_16 ? register_1_q : 8'bz;  // Controlled_Buffer controlled_buffer_3
  assign controlled_buffer_2_out = in_15 ? register_1_q : 8'bz;  // Controlled_Buffer controlled_buffer_4
  Register register_1 (.D(out_19), .en(in_10), .Q(register_1_q), .clk(in_13), .clr(in_14));
  Register register_2 (.D(out_19), .en(in_12), .Q(register_2_q), .clk(in_13), .clr(in_14));
  assign controlled_buffer_2_out = in_17 ? register_2_q : 8'bz;  // Controlled_Buffer controlled_buffer_5
  assign controlled_buffer_2_out = in_18 ? register_2_q : 8'bz;  // Controlled_Buffer controlled_buffer_6
  new_alu new_alu_1 (
    .a(controlled_buffer_2_out), .in_2(in_3), .b(controlled_buffer_1_out), .in_4(in_4), .\and (in_5),
    .\or (in_6), .exor(in_8), .lsl(in_9), .rsl(in_11), .out_10(out_19), .out_11(out_20));
endmodule

module latch (
  input  D,
  input  enable,
  input  _1_45_12,
  output out_4
);

  wire and_1_out, and_2_out, nor_1_out, not_1_out, or_1_out;

  and and_1 (and_1_out, enable, not_1_out);
  not not_1 (not_1_out, D);
  and and_2 (and_2_out, D, enable);
  or or_1 (or_1_out, and_1_out, _1_45_12);
  nor nor_1 (nor_1_out, and_2_out, out_4);
  nor nor_2 (out_4, nor_1_out, or_1_out);
endmodule

module edge_triggered_flip_flop (
  input  in_1,
  input  in_2,
  input  in_3,
  output out_4
);

  wire latch_1_out_4, not_1_out, not_2_out;

  not not_1 (not_1_out, in_2);
  latch latch_1 (.D(in_1), .enable(not_1_out), .out_4(latch_1_out_4), ._1_45_12(in_3));
  not not_2 (not_2_out, not_1_out);
  latch latch_2 (.D(latch_1_out_4), .enable(not_2_out), .out_4(out_4), ._1_45_12(in_3));
endmodule
